# Fritzing sketch Smart-Irrigation-Circuit (saved by Fritzing 0.9.3b)
breadboards: 1

parts:
  Parça1 = Arduino Uno (Rev3) - ICSP
  Parça2 = HC-05 [part_number=HC-05 package="breakout board"]
  Water_Level_Sensor1 = Water Level Sensor
  L298N2 = L298N DC motor driver
  부품3 = FC-28 Soil Hygrometer Module
  부품4 = FC-28 Soil Hygrometer Module - Probe
  M3 = DC Motor
  VCC1 = Battery block 9V
  R1 = Resistor [tolerance=±5% resistance=1k package=THT]
  R2 = Resistor [tolerance=±5% resistance=1k package=THT]
  R4 = Resistor [tolerance=±5% resistance=1k package=THT]
  R5 = Resistor [tolerance=±5% resistance=1k package=THT]
  LED1 = LED - 5mm [color="Red (633nm)" package="5 mm [THT]"]
  LED2 = LED - 5mm [color="Green (570nm)" package="5 mm [THT]"]

nets:
  N1: Parça1.A0, 부품3.AO
  N2: Parça1.A1, Water_Level_Sensor1.SIG
  N3: Parça1.D8, R4.Pin_1, LED1.anode
  N4: Parça1.D9_PWM, R5.Pin_1, LED2.anode
  N5: Parça1.D0/RX, Parça2.TXD
  N6: Parça1.D1/TX, R1.Pin_1
  N7: Parça1.D3_PWM, L298N2.ENA
  N8: Parça1.D5_PWM, L298N2.IN1
  N9: Parça1.D6_PWM, L298N2.IN2
  VCC: Parça1.5V, Parça2.VCC, Water_Level_Sensor1.VCC, 부품3.VCC, R4.Pin_0, R5.Pin_0
  GND: Parça1.GND, Parça2.GND, Water_Level_Sensor1.GND, 부품3.GND, LED1.cathode, LED2.cathode
  N10: Parça2.RXD, R2.Pin_1
  N11: L298N2.OUT2, M3.pin_1, M3.pin_2
  N12: L298N2.12V, VCC1.+
  N13: L298N2.GND, VCC1.-
  N14: 부품3.POS, 부품4.POS
  N15: 부품3.NEG, 부품4.NEG
  N16: R1.Pin_0, R2.Pin_0

custom parts:
  HC-05: A commonly available HC-05 Bluetooth breakout board.
  Water Level Sensor: A water level sensor. This sensor operates at 3V to 5V. The Sig (signal) pin outputs an analogue signal that is in proportion to the amount of water in contact with the sensor.
  L298N DC motor driver: 2x DC motor driver with 78M05 positive voltage regulator (7..35 V) L298N: max 46 V, 2 A Set 5 V Enable jumper to enable 5 V regultor (needed for the L298N) and +5 V output at screw terminal or supply external +5 V at screw terminal Set ENA and/or ENB to +5 V to enable motor permanently or supply ENA and/or ENB with PWM signal IN1 and IN2 set rotation directory for motor A (OUT1/OUT2) IN2 and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
  FC-28 Soil Hygrometer Module: The FC-28 is a soil hygrometer module that uses the Texas Instruments LM393 comparator chip to provide an analog measurement of soil humidity. The digital output is high when soil moisture is over a certain threshold, as determined by adjusting the potentiometer.
  FC-28 Soil Hygrometer Module - Probe: The FC-28 is a soil hygrometer module that uses the Texas Instruments LM393 comparator chip to provide an analog measurement of soil humidity.
